# Fritzing sketch mp3_player (saved by Fritzing 0.9.3b)
breadboards: 1

parts:
  Raspberry_Pi_1 = Raspberry Pi 3 [part_number=RPI-3-V1.2]
  S1 = Pushbutton [package="[SMD]"]
  S2 = Pushbutton [package="[SMD]"]
  S3 = Pushbutton [package="[SMD]"]
  S4 = Pushbutton [package="[SMD]"]
  S5 = Pushbutton [package="[SMD]"]
  S6 = Pushbutton [package="[SMD]"]
  IC1 = IC, DIP package, 16 pins [chip_label=MCP3008]  # not connected
  R1 = Trimmer Potentiometer [maximum_resistance=10kΩ package=THT]  # not connected
  R2 = Trimmer Potentiometer [maximum_resistance=10kΩ package=THT]  # not connected

nets:
  N1: Raspberry_Pi_1.ID_SD, S1.Pin_3, S1.Pin_4
  N2: Raspberry_Pi_1.GIPO5, S2.Pin_3, S2.Pin_4
  N3: Raspberry_Pi_1.GIPO6, S3.Pin_3, S3.Pin_4
  N4: Raspberry_Pi_1.GIPO13, S4.Pin_3, S4.Pin_4
  N5: Raspberry_Pi_1.GIPO19, S5.Pin_3, S5.Pin_4
  N6: Raspberry_Pi_1.GIPO26, S6.Pin_3, S6.Pin_4
  N7: Raspberry_Pi_1.GND, S1.Pin_1, S1.Pin_2, S2.Pin_1, S2.Pin_2, S3.Pin_1, S3.Pin_2, S4.Pin_1, S4.Pin_2, S5.Pin_1, S5.Pin_2, S6.Pin_1, S6.Pin_2
